// Digital circuit P11.dig as structural Verilog
module P11 (
  input  we,
  input  [4:0] rd,
  output [31:0] wen
);

  wire d_0_0, d_0_1, d_0_2, d_0_3, d_0_4, d_0_5, d_0_6, d_0_7, d_1_0, d_1_1, d_1_2, d_1_3, d_1_4, d_1_5,
       d_1_6, d_1_7, d_2_0, d_2_1, d_2_2, d_2_3, d_2_4, d_2_5, d_2_6, d_2_7, d_3_0, d_3_1, d_3_2, d_3_3,
       d_3_4, d_3_5, d_3_6, d_3_7, g0, g1, g2, g3;

  Decoder #(.Selector_Bits(2)) decoder_1 (.out_0(g0), .out_1(g1), .out_2(g2), .out_3(g3));  // open: sel
  Decoder #(.Selector_Bits(3)) decoder_2 (
    .out_0(d_0_0), .out_1(d_0_1), .out_2(d_0_2), .out_3(d_0_3), .out_4(d_0_4), .out_5(d_0_5), .out_6(d_0_6),
    .out_7(d_0_7));  // open: sel
  Decoder #(.Selector_Bits(3)) decoder_3 (
    .out_0(d_1_0), .out_1(d_1_1), .out_2(d_1_2), .out_3(d_1_3), .out_4(d_1_4), .out_5(d_1_5), .out_6(d_1_6),
    .out_7(d_1_7));  // open: sel
  Decoder #(.Selector_Bits(3)) decoder_4 (
    .out_0(d_2_0), .out_1(d_2_1), .out_2(d_2_2), .out_3(d_2_3), .out_4(d_2_4), .out_5(d_2_5), .out_6(d_2_6),
    .out_7(d_2_7));  // open: sel
  Decoder #(.Selector_Bits(3)) decoder_5 (
    .out_0(d_3_0), .out_1(d_3_1), .out_2(d_3_2), .out_3(d_3_3), .out_4(d_3_4), .out_5(d_3_5), .out_6(d_3_6),
    .out_7(d_3_7));  // open: sel
  and and_1 (wen[1], we, g0, d_0_1);
  and and_2 (wen[2], we, g0, d_0_2);
  and and_3 (wen[3], we, g0, d_0_3);
  and and_4 (wen[4], we, g0, d_0_4);
  and and_5 (wen[5], we, g0, d_0_5);
  and and_6 (wen[6], we, g0, d_0_6);
  and and_7 (wen[7], we, g0, d_0_7);
  and and_8 (wen[8], we, g1, d_1_0);
  and and_9 (wen[9], we, g1, d_1_1);
  and and_10 (wen[10], we, g1, d_1_2);
  and and_11 (wen[11], we, g1, d_1_3);
  and and_12 (wen[12], we, g1, d_1_4);
  and and_13 (wen[13], we, g1, d_1_5);
  and and_14 (wen[14], we, g1, d_1_6);
  and and_15 (wen[15], we, g1, d_1_7);
  and and_16 (wen[16], we, g2, d_2_0);
  and and_17 (wen[17], we, g2, d_2_1);
  and and_18 (wen[18], we, g2, d_2_2);
  and and_19 (wen[19], we, g2, d_2_3);
  and and_20 (wen[20], we, g2, d_2_4);
  and and_21 (wen[21], we, g2, d_2_5);
  and and_22 (wen[22], we, g2, d_2_6);
  and and_23 (wen[23], we, g2, d_2_7);
  and and_24 (wen[24], we, g3, d_3_0);
  and and_25 (wen[25], we, g3, d_3_1);
  and and_26 (wen[26], we, g3, d_3_2);
  and and_27 (wen[27], we, g3, d_3_3);
  and and_28 (wen[28], we, g3, d_3_4);
  and and_29 (wen[29], we, g3, d_3_5);
  and and_30 (wen[30], we, g3, d_3_6);
  and and_31 (wen[31], we, g3, d_3_7);

  assign wen[0] = 1'b0;

  // Other names for the same wires on the sheet: rd_lo[2:0] = rd[2:0]; rd_hi[1:0] = rd[4:3]; w1 = wen[1]; w2 = wen[2];
  //   w3 = wen[3]; w4 = wen[4]; w5 = wen[5]; w6 = wen[6]; w7 = wen[7]; w8 = wen[8]; w9 = wen[9]; w10 = wen[10];
  //   w11 = wen[11]; w12 = wen[12]; w13 = wen[13]; w14 = wen[14]; w15 = wen[15]; w16 = wen[16]; w17 = wen[17];
  //   w18 = wen[18]; w19 = wen[19]; w20 = wen[20]; w21 = wen[21]; w22 = wen[22]; w23 = wen[23]; w24 = wen[24];
  //   w25 = wen[25]; w26 = wen[26]; w27 = wen[27]; w28 = wen[28]; w29 = wen[29]; w30 = wen[30]; w31 = wen[31]
endmodule
