// Digital circuit P23.dig as structural Verilog
module P23 (
  input  [4:0] op_hi,
  output [15:0] ctrl
);

  ROM #(.AddrBits(5), .Bits(16)) rom_1 (.A(op_hi), .sel(1'b1), .D(ctrl));

  // Notes on the sheet:
  //   P23 Microprogrammed control (control ROM) - Digital task
  //   Full size: a ROM part (5 address bits, 16 data bits); you work out and enter the contents.
  //   Allowed parts: gates + multiplexer/decoder parts + ROM
  //   Do not rename, move or delete the input and output pins.
  //   contents of rom_1 (hex, n*v repeats v):
  //   5480,0,0,0,5000,7030,0,0,1210,0,0,0,4000,5830,10*0,28,5102,0,4144,4181
endmodule

/* Test case public tests:
op_hi ctrl
0 21632
1 0
2 0
3 0
4 20480
5 28720
6 0
7 0
8 4624
9 0
10 0
11 0
12 16384
13 22576
14 0
15 0
16 0
17 0
18 0
19 0
20 0
21 0
22 0
23 0
24 40
25 20738
26 0
27 16708
28 16769
29 0
30 0
31 0
*/
