// Digital circuit P29.dig as structural Verilog
module P29 (
  input  clk,
  input  we,
  input  [1:0] addr,
  input  [7:0] wdata,
  output [7:0] rdata
);

  wire and_1_out, and_2_out, and_3_out, and_4_out, decoder_1_out_0, decoder_1_out_1, decoder_1_out_2,
       decoder_1_out_3;
  wire [7:0] d_ff_1_q, d_ff_2_q, d_ff_3_q, d_ff_4_q, multiplexer_1_out, multiplexer_2_out, multiplexer_3_out,
       multiplexer_4_out;

  Multiplexer #(.Bits(8)) multiplexer_1 (.sel(and_1_out), .in_0(d_ff_1_q), .in_1(wdata), .out(multiplexer_1_out));
  Multiplexer #(.Bits(8)) multiplexer_2 (.sel(and_2_out), .in_0(d_ff_2_q), .in_1(wdata), .out(multiplexer_2_out));
  Multiplexer #(.Bits(8)) multiplexer_3 (.sel(and_3_out), .in_0(d_ff_3_q), .in_1(wdata), .out(multiplexer_3_out));
  Multiplexer #(.Bits(8)) multiplexer_4 (.sel(and_4_out), .in_0(d_ff_4_q), .in_1(wdata), .out(multiplexer_4_out));
  Decoder #(.Selector_Bits(2)) decoder_1 (
    .sel(addr), .out_0(decoder_1_out_0), .out_1(decoder_1_out_1), .out_2(decoder_1_out_2),
    .out_3(decoder_1_out_3));
  D_FF #(.Bits(8)) d_ff_1 (.D(multiplexer_1_out), .C(clk), .Q(d_ff_1_q));  // open: nQ
  D_FF #(.Bits(8)) d_ff_2 (.D(multiplexer_2_out), .C(clk), .Q(d_ff_2_q));  // open: nQ
  D_FF #(.Bits(8)) d_ff_3 (.D(multiplexer_3_out), .C(clk), .Q(d_ff_3_q));  // open: nQ
  D_FF #(.Bits(8)) d_ff_4 (.D(multiplexer_4_out), .C(clk), .Q(d_ff_4_q));  // open: nQ
  and and_1 (and_1_out, decoder_1_out_0, we);
  and and_2 (and_2_out, decoder_1_out_1, we);
  and and_3 (and_3_out, decoder_1_out_2, we);
  and and_4 (and_4_out, decoder_1_out_3, we);
  Multiplexer #(.Bits(8), .Selector_Bits(2)) multiplexer_5 (
    .sel(addr), .in_0(d_ff_1_q), .in_1(d_ff_2_q), .in_2(d_ff_3_q), .in_3(d_ff_4_q), .out(rdata));

  // Notes on the sheet:
  //   clk: Hz: 1
  //   P29 Data memory - Digital task
  //   4 words x 8 bits from D flip-flops: address decoder for writing, multiplexer for reading.
  //   Allowed parts: gates + multiplexer/decoder parts + flip-flops
  //   Do not rename, move or delete the input and output pins.
endmodule

/* Test case public tests:
clk we addr wdata rdata
C 1 1 255 255
C 0 3 41 X
C 0 0 255 X
C 0 1 165 255
C 0 0 127 X
C 0 1 177 255
C 0 0 113 X
C 0 1 207 255
C 1 2 26 26
C 1 1 11 11
C 1 2 236 236
C 1 3 126 126
C 1 1 7 7
C 1 2 30 30
C 0 3 68 126
C 1 0 12 12
C 0 1 15 7
C 1 2 191 191
C 0 2 30 191
C 1 1 9 9
C 1 2 0 0
C 0 2 103 0
C 1 0 148 148
C 0 1 22 9
C 0 3 195 126
C 1 2 40 40
C 0 1 255 9
C 1 1 127 127
C 0 3 84 126
C 1 0 197 197
C 0 0 182 197
C 0 1 127 127
C 0 2 127 40
C 0 1 255 127
C 0 2 26 40
C 1 3 25 25
C 0 1 6 127
C 0 1 0 127
C 0 0 30 197
C 0 3 127 25
C 0 3 106 25
C 0 2 31 40
C 0 1 125 127
C 1 2 0 0
C 1 2 29 29
C 1 1 231 231
C 0 2 22 29
C 1 3 183 183
C 1 1 192 192
C 0 0 81 197
C 1 0 231 231
C 1 2 128 128
C 1 3 23 23
C 0 2 255 128
C 0 3 255 23
C 0 0 39 231
C 0 1 0 192
C 1 0 13 13
C 0 3 128 23
C 0 2 51 128
C 0 3 250 23
C 1 3 128 128
C 0 0 0 13
C 1 1 226 226
C 1 0 122 122
C 1 1 255 255
C 0 2 255 128
C 0 1 242 255
C 0 0 105 122
C 1 3 128 128
C 1 1 0 0
C 1 3 86 86
C 0 1 163 0
C 0 3 255 86
C 0 0 194 122
C 1 3 128 128
C 1 0 128 128
C 0 1 0 0
C 0 3 255 128
C 1 2 194 194
C 1 3 250 250
C 1 0 178 178
C 1 1 5 5
C 0 1 25 5
C 0 1 127 5
C 0 2 1 194
C 1 0 48 48
C 0 2 158 194
C 0 2 0 194
C 1 1 255 255
C 1 1 21 21
C 0 0 203 48
C 0 2 127 194
C 1 1 0 0
C 0 3 127 250
C 1 3 29 29
C 0 1 120 0
C 1 1 255 255
C 0 0 216 48
C 0 3 66 29
C 1 2 251 251
C 1 1 138 138
C 1 2 18 18
C 1 1 128 128
C 1 2 6 6
C 1 3 17 17
C 0 2 116 6
C 1 3 190 190
C 0 2 2 6
C 1 1 0 0
C 1 2 52 52
C 0 1 255 0
C 0 2 166 52
C 1 2 205 205
C 0 0 127 48
C 0 3 70 190
C 0 2 140 205
C 0 2 127 205
C 0 0 23 48
C 0 2 255 205
C 0 3 181 190
C 1 0 253 253
C 1 2 58 58
C 1 3 143 143
C 0 3 255 143
C 1 2 20 20
C 0 2 29 20
C 0 3 127 143
C 1 3 128 128
C 1 1 0 0
C 0 1 28 0
C 1 2 127 127
C 1 0 119 119
C 0 3 147 128
C 0 3 136 128
C 0 3 1 128
C 1 2 127 127
C 0 0 27 119
C 1 0 218 218
C 0 2 255 127
C 1 0 155 155
C 0 1 128 0
C 0 3 236 128
C 0 0 243 155
C 1 2 179 179
C 0 2 12 179
C 1 1 193 193
C 0 3 255 128
C 1 0 130 130
C 1 3 128 128
C 1 1 94 94
C 1 3 200 200
C 1 2 0 0
C 1 2 18 18
C 0 2 222 18
C 0 2 1 18
C 1 1 209 209
C 0 2 238 18
C 1 0 0 0
C 1 3 60 60
*/
