// Digital circuit P44.dig as structural Verilog
module P44 (
  input  [3:0] hex,
  output [6:0] seg
);

  wire An, and_1_out, and_2_out, and_3_out, and_4_out, and_5_out, and_6_out, and_7_out, and_8_out, and_9_out,
       and_10_out, and_11_out, and_12_out, and_13_out, and_14_out, and_15_out, and_16_out, and_17_out,
       and_18_out, and_19_out, and_20_out, and_21_out, and_22_out, and_23_out, and_24_out, and_25_out,
       and_26_out, and_27_out, and_28_out, and_29_out, and_30_out, and_31_out, and_32_out, and_33_out,
       and_34_out, and_35_out, Bn, Cn, Dn;

  not not_1 (Dn, hex[0]);
  not not_2 (Cn, hex[1]);
  not not_3 (Bn, hex[2]);
  not not_4 (An, hex[3]);
  and and_1 (and_1_out, Bn, Dn);
  and and_2 (and_2_out, hex[2], hex[1]);
  and and_3 (and_3_out, An, hex[1]);
  and and_4 (and_4_out, An, hex[2], hex[0]);
  and and_5 (and_5_out, hex[3], Dn);
  and and_6 (and_6_out, hex[3], Bn, Cn);
  and and_7 (and_7_out, Bn, Dn);
  and and_8 (and_8_out, Bn, Cn);
  and and_9 (and_9_out, An, Cn, Dn);
  and and_10 (and_10_out, An, hex[1], hex[0]);
  and and_11 (and_11_out, hex[3], Cn, hex[0]);
  and and_12 (and_12_out, Cn, hex[0]);
  and and_13 (and_13_out, Bn, hex[0]);
  and and_14 (and_14_out, Bn, Cn);
  and and_15 (and_15_out, An, hex[2]);
  and and_16 (and_16_out, hex[3], Bn);
  and and_17 (and_17_out, Bn, hex[1], hex[0]);
  and and_18 (and_18_out, hex[2], Cn, hex[0]);
  and and_19 (and_19_out, hex[2], hex[1], Dn);
  and and_20 (and_20_out, An, Bn, Dn);
  and and_21 (and_21_out, hex[3], Cn);
  and and_22 (and_22_out, hex[1], Dn);
  and and_23 (and_23_out, Bn, Dn);
  and and_24 (and_24_out, hex[3], hex[1]);
  and and_25 (and_25_out, hex[3], hex[2]);
  and and_26 (and_26_out, Cn, Dn);
  and and_27 (and_27_out, hex[2], Dn);
  and and_28 (and_28_out, An, hex[2], Cn);
  and and_29 (and_29_out, hex[3], hex[1]);
  and and_30 (and_30_out, hex[3], Bn);
  and and_31 (and_31_out, hex[1], Dn);
  and and_32 (and_32_out, Bn, hex[1]);
  and and_33 (and_33_out, An, hex[2], Cn);
  and and_34 (and_34_out, hex[3], hex[0]);
  and and_35 (and_35_out, hex[3], Bn);
  or or_1 (seg[0], and_1_out, and_2_out, and_3_out, and_4_out, and_5_out, and_6_out);
  or or_2 (seg[1], and_7_out, and_8_out, and_9_out, and_10_out, and_11_out);
  or or_3 (seg[2], and_12_out, and_13_out, and_14_out, and_15_out, and_16_out);
  or or_4 (seg[3], and_17_out, and_18_out, and_19_out, and_20_out, and_21_out);
  or or_5 (seg[4], and_22_out, and_23_out, and_24_out, and_25_out);
  or or_6 (seg[5], and_26_out, and_27_out, and_28_out, and_29_out, and_30_out);
  or or_7 (seg[6], and_31_out, and_32_out, and_33_out, and_34_out, and_35_out);

  // Other names for the same wires on the sheet: D = hex[0]; C = hex[1]; B = hex[2]; A = hex[3]; seg_a = seg[0];
  //   seg_b = seg[1]; seg_c = seg[2]; seg_d = seg[3]; seg_e = seg[4]; seg_f = seg[5]; seg_g = seg[6]

  // Notes on the sheet:
  //   P44 Seven-segment decoder - Digital task
  //   Full size, gates only: seven 4-variable K-maps, one per segment.
  //   Allowed parts: And, Or, Not, NAnd, NOr, XOr, XNOr + wiring parts
  //   Do not rename, move or delete the input and output pins.
endmodule

/* Test case public tests:
hex seg
0 63
1 6
2 91
3 79
4 102
5 109
6 125
7 7
8 127
9 111
10 119
11 124
12 57
13 94
14 121
15 113
*/
