// Digital circuit P50.dig as structural Verilog
module P50 (
  input  [7:0] clk,
  input  rst,
  input  start,
  input  [3:0] a,
  input  [3:0] b,
  output [7:0] result,
  output busy
);

  wire b_lsb, comparator_1_eq, done, load, not_1_out;
  wire [2:0] add_2_s, multiplexer_1_out, multiplexer_2_out, multiplexer_6_out, register_3_q, undriven_4,
       undriven_5;
  wire [3:0] undriven;
  wire [3:1] register_1_q;
  wire [7:0] add_1_s, multiplexer_3_out, multiplexer_7_out, multiplexer_9_out, reg_a, undriven_2, undriven_3,
       undriven_6;

  Multiplexer #(.Bits(3)) multiplexer_1 (.sel(start), .in_0(3'b000), .in_1(3'b001), .out(multiplexer_1_out));
  Multiplexer #(.Bits(3)) multiplexer_2 (.sel(done), .in_0(add_2_s), .in_1(3'b000), .out(multiplexer_2_out));
  not not_1 (not_1_out, busy);
  Multiplexer #(.Bits(8)) multiplexer_3 (.sel(b_lsb), .in_0({8{1'b0}}), .in_1(reg_a), .out(multiplexer_3_out));
  and and_1 (load, not_1_out, start);
  Multiplexer #(.Bits(4)) multiplexer_4 (.sel(load), .in_0({1'b0, register_1_q}), .in_1(b), .out(clk[3:0]));
  Multiplexer #(.Bits(8)) multiplexer_5 (.sel(load), .in_0({reg_a[6:0], 1'b0}), .in_1({4'b0000, a}), .out(clk));
  Add #(.Bits(8)) add_1 (.a(result), .b(multiplexer_3_out), .c_i(multiplexer_3_out[0]), .s(add_1_s));  // open: c_o
  Multiplexer #(.Bits(3)) multiplexer_6 (
    .sel(busy), .in_0(multiplexer_1_out), .in_1(multiplexer_2_out), .out(multiplexer_6_out));
  Register #(.Bits(4)) register_1 (.D(undriven), .C(clk[0]), .en(1'b1), .Q({register_1_q, b_lsb}));
  Register #(.Bits(8)) register_2 (.D(undriven_2), .C(clk[0]), .en(1'b1), .Q(reg_a));
  Multiplexer #(.Bits(8)) multiplexer_7 (.sel(busy), .in_0(undriven_3), .in_1(add_1_s), .out(multiplexer_7_out));
  Multiplexer #(.Bits(3)) multiplexer_8 (.sel(rst), .in_0(multiplexer_6_out), .in_1(3'b000), .out(clk[2:0]));
  Register #(.Bits(3)) register_3 (.D(clk[2:0]), .C(clk[0]), .en(1'b1), .Q(register_3_q));
  Multiplexer #(.Bits(8)) multiplexer_9 (
    .sel(load), .in_0(multiplexer_7_out), .in_1({8{1'b0}}), .out(multiplexer_9_out));
  Multiplexer #(.Bits(8)) multiplexer_10 (.sel(rst), .in_0(multiplexer_9_out), .in_1({8{1'b0}}), .out(clk));
  Add #(.Bits(3)) add_2 (.a(undriven_4), .b(3'b001), .c_i(1'b0), .s(add_2_s));  // open: c_o
  Comparator #(.Bits(3)) comparator_1 (.a(undriven_5), .b(3'b000), .eq(comparator_1_eq));  // open: gt, lt
  Comparator #(.Bits(3)) comparator_2 (.a(undriven_4), .b(3'b100), .eq(done));  // open: gt, lt
  Register #(.Bits(8)) register_4 (.D(undriven_6), .C(clk[0]), .en(1'b1), .Q(result));
  not not_2 (busy, comparator_1_eq);
  // Pins of 1 and 3 and 4 and 8 bits meet at clk
  // Pins of 1 and 8 bits meet at multiplexer_3_out
  // also tied to GND on the sheet: multiplexer_3_out[0]

  // Other names for the same wires on the sheet: res[7:0] = result

  // Notes on the sheet:
  //   clk: Hz: 1
endmodule

/* Test case public tests:
clk rst start a b result busy
C 1 1 7 4 0 0
C 0 1 12 2 0 1
C 0 0 8 0 0 1
C 0 1 2 11 24 1
C 0 1 2 14 24 1
C 0 1 15 2 24 0
C 0 1 8 4 0 1
C 0 0 13 10 0 1
C 0 0 6 0 0 1
C 0 1 8 11 32 1
C 0 0 3 14 32 0
C 0 1 0 7 0 1
C 0 0 13 10 0 1
C 0 1 8 9 0 1
C 0 0 2 12 0 1
C 0 0 7 7 0 0
C 0 0 0 5 0 0
C 0 1 8 10 0 1
C 0 1 9 3 0 1
C 0 0 11 7 16 1
C 0 0 0 6 16 1
C 0 0 14 10 80 0
C 0 0 11 10 80 0
C 0 0 15 7 80 0
C 0 0 8 1 80 0
C 0 1 0 3 0 1
C 0 1 11 8 0 1
C 0 0 8 13 0 1
C 0 1 7 11 0 1
C 0 1 4 8 0 0
C 0 1 7 10 0 1
C 0 0 6 12 0 1
C 0 1 14 11 14 1
C 0 1 8 13 14 1
C 0 0 14 12 70 0
C 0 0 13 15 70 0
C 0 0 3 6 70 0
C 0 0 15 9 70 0
C 0 0 8 7 70 0
C 0 0 3 11 70 0
C 0 0 15 13 70 0
C 0 1 2 6 0 1
C 0 1 7 13 0 1
C 0 0 4 3 4 1
C 0 0 14 7 12 1
C 0 1 8 10 12 0
C 0 1 8 14 0 1
C 0 0 15 11 0 1
C 0 1 8 0 16 1
C 0 0 15 9 48 1
C 0 1 0 8 112 0
C 0 0 14 5 112 0
C 0 1 5 0 0 1
C 0 1 13 15 0 1
C 0 0 10 0 0 1
C 0 1 1 4 0 1
C 0 0 10 7 0 0
C 0 0 15 8 0 0
C 0 0 3 9 0 0
C 0 1 11 6 0 1
C 0 1 15 1 0 1
C 1 0 8 8 0 0
C 0 1 3 12 0 1
C 0 1 1 8 0 1
C 0 0 8 8 0 1
C 0 0 8 9 12 1
C 0 0 8 14 36 0
C 0 0 4 9 36 0
C 0 1 15 1 0 1
C 0 0 7 0 15 1
C 0 1 10 3 15 1
C 0 0 6 9 15 1
C 0 1 5 9 15 0
C 0 1 12 0 0 1
C 0 1 14 14 0 1
C 0 1 3 6 0 1
C 0 0 15 5 0 1
C 0 1 6 0 0 0
C 0 1 2 8 0 1
C 0 0 8 15 0 1
C 1 1 7 13 0 0
C 0 1 7 14 0 1
C 0 0 15 0 0 1
C 0 0 4 2 14 1
C 0 0 7 15 42 1
C 0 1 7 0 98 0
C 1 0 1 15 0 0
C 0 0 13 0 0 0
C 0 0 13 1 0 0
C 0 0 4 15 0 0
C 0 1 15 8 0 1
C 0 0 0 8 0 1
C 0 0 9 0 0 1
C 0 1 11 11 0 1
C 0 0 7 7 120 0
C 0 1 8 0 0 1
C 0 1 5 2 0 1
C 0 1 3 7 0 1
C 0 1 2 13 0 1
C 0 0 8 11 0 0
C 0 1 6 14 0 1
C 0 0 2 5 0 1
C 0 1 9 6 12 1
C 0 0 15 13 36 1
C 0 0 0 13 84 0
C 0 0 15 4 84 0
C 0 0 7 12 84 0
C 0 1 6 1 0 1
C 0 1 7 0 6 1
C 0 1 0 8 6 1
C 0 0 7 7 6 1
C 0 0 4 0 6 0
C 0 1 8 0 0 1
C 0 0 1 7 0 1
C 0 0 15 4 0 1
C 0 1 11 1 0 1
C 0 1 10 15 0 0
C 0 1 0 0 0 1
C 0 0 13 15 0 1
C 0 1 1 5 0 1
C 0 0 10 1 0 1
C 0 0 3 8 0 0
C 0 1 15 8 0 1
C 0 0 15 6 0 1
C 0 1 13 0 0 1
C 0 1 6 10 0 1
C 0 1 6 11 120 0
C 0 1 0 8 0 1
C 0 0 8 13 0 1
C 0 0 9 1 0 1
C 0 1 2 8 0 1
C 1 1 15 13 0 0
C 0 0 8 14 0 0
C 0 0 12 8 0 0
C 0 1 14 13 0 1
C 0 1 2 7 14 1
C 0 1 2 7 14 1
C 0 1 15 0 70 1
C 0 0 7 1 182 0
C 0 1 14 0 0 1
C 0 0 14 14 0 1
C 0 0 6 1 0 1
C 0 0 14 15 0 1
C 0 1 8 7 0 0
C 0 1 15 9 0 1
C 0 1 8 13 15 1
C 0 1 9 8 15 1
C 0 1 15 12 15 1
C 0 1 5 15 135 0
C 0 0 15 7 135 0
C 0 0 13 12 135 0
C 0 1 15 2 0 1
C 0 0 8 1 0 1
C 0 0 13 7 30 1
C 0 0 0 0 30 1
C 0 0 7 0 30 0
C 0 0 12 8 30 0
C 0 1 8 9 0 1
C 0 1 5 10 8 1
C 1 0 3 1 0 0
*/
