// Digital circuit P53.dig as structural Verilog
module P53 (
  input  clk,
  input  rst,
  input  en,
  input  kick,
  input  [7:0] load,
  output [7:0] count,
  output bite
);

  wire and_1_out, and_2_out, and_3_out, comparator_1_eq, not_1_out, not_2_out, or_1_out;
  wire [7:0] multiplexer_1_out, multiplexer_2_out, multiplexer_3_out, multiplexer_4_out, sub_1_s;

  Comparator #(.Bits(8)) comparator_1 (.a(count), .b({8{1'b0}}), .eq(comparator_1_eq));  // open: gt, lt
  Sub #(.Bits(8)) sub_1 (.a(count), .b(8'h1), .c_i(1'b0), .s(sub_1_s));  // open: c_o
  not not_1 (not_1_out, rst);
  Multiplexer #(.Bits(8)) multiplexer_1 (.sel(comparator_1_eq), .in_0(sub_1_s), .in_1(load), .out(multiplexer_1_out));
  and and_1 (and_1_out, en, comparator_1_eq);
  not not_2 (not_2_out, kick);
  Multiplexer #(.Bits(8)) multiplexer_2 (.sel(en), .in_0(count), .in_1(multiplexer_1_out), .out(multiplexer_2_out));
  and and_2 (and_2_out, and_1_out, not_2_out);
  Multiplexer #(.Bits(8)) multiplexer_3 (.sel(kick), .in_0(multiplexer_2_out), .in_1(load), .out(multiplexer_3_out));
  or or_1 (or_1_out, and_2_out, bite);
  Register #(.Bits(8)) register_1 (.D(multiplexer_4_out), .C(clk), .en(1'b1), .Q(count));
  Multiplexer #(.Bits(8)) multiplexer_4 (
    .sel(rst), .in_0(multiplexer_3_out), .in_1({8{1'b0}}), .out(multiplexer_4_out));
  and and_3 (and_3_out, or_1_out, not_1_out);
  D_FF d_ff_1 (.D(and_3_out), .C(clk), .Q(bite));  // open: nQ

  // Notes on the sheet:
  //   clk: Hz: 1
  //   P53 Watchdog timer - Digital task
  //   8-bit down counter with reload and the sticky bite flag.
  //   Allowed parts: all of the above + Add, Sub, Comparator, Neg
  //   Do not rename, move or delete the input and output pins.
endmodule

/* Test case public tests:
clk rst en kick load count bite
C 1 1 1 243 0 0
C 0 1 1 84 84 0
C 0 1 0 254 83 0
C 0 1 1 40 40 0
C 0 1 1 209 209 0
C 0 0 0 8 209 0
C 0 0 0 109 209 0
C 0 1 1 0 0 0
C 0 0 0 0 0 0
C 0 1 0 127 127 1
C 0 0 1 26 26 1
C 0 0 1 12 12 1
C 0 1 1 31 31 1
C 0 0 0 222 31 1
C 0 1 1 127 127 1
C 0 1 0 0 126 1
C 0 1 1 203 203 1
C 0 0 1 0 0 1
C 0 1 1 26 26 1
C 0 0 1 28 28 1
C 0 0 0 0 28 1
C 0 1 1 138 138 1
C 0 0 0 150 138 1
C 1 1 1 31 0 0
C 0 1 0 89 89 1
C 0 0 0 2 89 1
C 0 0 1 209 209 1
C 0 0 1 223 223 1
C 0 1 1 239 239 1
C 0 0 1 0 0 1
C 0 1 0 67 67 1
C 0 0 1 94 94 1
C 0 0 1 252 252 1
C 0 0 0 0 252 1
C 0 1 0 113 251 1
C 0 1 1 5 5 1
C 0 1 0 158 4 1
C 0 1 1 128 128 1
C 0 0 1 128 128 1
C 0 0 0 147 128 1
C 0 1 1 127 127 1
C 0 1 1 16 16 1
C 0 0 0 164 16 1
C 0 0 0 31 16 1
C 0 0 0 0 16 1
C 0 0 0 147 16 1
C 0 0 0 11 16 1
C 0 0 0 11 16 1
C 0 0 0 215 16 1
C 0 1 0 127 15 1
C 0 0 0 1 15 1
C 0 0 0 6 15 1
C 0 1 0 101 14 1
C 0 1 0 7 13 1
C 0 1 0 139 12 1
C 0 0 1 255 255 1
C 0 1 1 16 16 1
C 0 1 1 99 99 1
C 0 1 0 76 98 1
C 0 1 1 10 10 1
C 0 0 0 19 10 1
C 0 0 1 233 233 1
C 0 0 0 107 233 1
C 0 0 0 127 233 1
C 0 0 1 241 241 1
C 0 0 1 255 255 1
C 0 0 1 147 147 1
C 0 1 0 75 146 1
C 0 0 0 71 146 1
C 0 1 1 255 255 1
C 0 0 1 127 127 1
C 0 0 0 28 127 1
C 0 0 0 128 127 1
C 0 1 0 35 126 1
C 0 1 1 0 0 1
C 0 0 1 128 128 1
C 0 1 0 128 127 1
C 0 1 1 151 151 1
C 0 1 0 3 150 1
C 0 0 1 249 249 1
C 0 1 0 174 248 1
C 0 0 1 48 48 1
C 0 0 0 153 48 1
C 0 0 0 21 48 1
C 0 0 0 255 48 1
C 0 0 0 253 48 1
C 0 1 0 16 47 1
C 0 0 0 255 47 1
C 0 1 0 12 46 1
C 0 0 0 60 46 1
C 0 1 1 128 128 1
C 0 0 0 243 128 1
C 0 0 0 0 128 1
C 0 1 1 119 119 1
C 0 1 0 129 118 1
C 0 0 0 74 118 1
C 0 0 1 247 247 1
C 0 1 1 5 5 1
C 0 0 1 0 0 1
C 0 0 0 21 0 1
C 0 1 1 56 56 1
C 0 0 1 0 0 1
C 0 1 0 0 0 1
C 0 0 1 42 42 1
C 1 0 1 255 0 0
C 0 1 0 255 255 1
C 0 1 0 20 254 1
C 0 0 1 128 128 1
C 0 0 1 7 7 1
C 0 1 1 128 128 1
C 0 1 1 255 255 1
C 0 0 0 15 255 1
C 0 0 1 11 11 1
C 0 1 1 104 104 1
C 0 1 0 23 103 1
C 0 0 0 178 103 1
C 0 1 0 127 102 1
C 0 0 1 19 19 1
C 0 1 1 127 127 1
C 0 0 1 7 7 1
C 0 0 0 0 7 1
C 0 1 0 0 6 1
C 0 0 1 26 26 1
C 0 1 1 128 128 1
C 0 0 0 0 128 1
C 0 0 1 68 68 1
C 0 1 1 217 217 1
C 0 1 0 92 216 1
C 0 0 0 20 216 1
C 0 1 1 156 156 1
C 0 1 1 18 18 1
C 0 1 0 31 17 1
C 0 0 0 0 17 1
C 0 1 1 95 95 1
C 0 0 0 112 95 1
C 0 1 0 142 94 1
C 0 1 0 26 93 1
C 0 0 1 125 125 1
C 0 0 1 58 58 1
C 0 0 0 31 58 1
C 0 0 1 127 127 1
C 0 1 0 0 126 1
C 0 1 1 255 255 1
C 0 1 1 71 71 1
C 0 1 0 2 70 1
C 0 0 1 33 33 1
C 0 1 0 15 32 1
C 0 0 0 1 32 1
C 0 0 0 72 32 1
C 0 0 1 62 62 1
C 0 1 0 9 61 1
C 0 0 1 20 20 1
C 0 0 0 11 20 1
C 0 0 1 158 158 1
C 0 1 1 197 197 1
C 0 1 1 18 18 1
C 0 0 0 198 18 1
C 0 1 1 232 232 1
C 0 1 0 145 231 1
C 0 0 1 9 9 1
*/
