// Digital circuit P60.dig as structural Verilog
module P60 (
  input  [31:0] data,
  output [4:0] parity,
  output [2:0] odd
);

  wire xor_13_out, xor_14_out;
  wire [1:0] xor_5_out, xor_6_out, xor_7_out, xor_8_out;
  wire [2:0] add_1_s, add_2_s;
  wire [3:0] xor_1_out, xor_2_out, xor_3_out, xor_4_out;

  assign xor_1_out = data[3:0] ^ data[7:4];  // XOr xor_1, 4 bits wide
  assign xor_2_out = data[11:8] ^ data[15:12];  // XOr xor_2, 4 bits wide
  assign xor_3_out = data[19:16] ^ data[23:20];  // XOr xor_3, 4 bits wide
  assign xor_4_out = data[27:24] ^ data[31:28];  // XOr xor_4, 4 bits wide
  assign xor_5_out = xor_1_out[1:0] ^ xor_1_out[3:2];  // XOr xor_5, 2 bits wide
  assign xor_6_out = xor_2_out[1:0] ^ xor_2_out[3:2];  // XOr xor_6, 2 bits wide
  assign xor_7_out = xor_3_out[1:0] ^ xor_3_out[3:2];  // XOr xor_7, 2 bits wide
  assign xor_8_out = xor_4_out[1:0] ^ xor_4_out[3:2];  // XOr xor_8, 2 bits wide
  xor xor_9 (parity[0], xor_5_out[0], xor_5_out[1]);
  xor xor_10 (parity[1], xor_6_out[0], xor_6_out[1]);
  xor xor_11 (parity[2], xor_7_out[0], xor_7_out[1]);
  xor xor_12 (parity[3], xor_8_out[0], xor_8_out[1]);
  xor xor_13 (xor_13_out, parity[0], parity[1]);
  xor xor_14 (xor_14_out, parity[2], parity[3]);
  xor xor_15 (parity[4], xor_13_out, xor_14_out);
  Add #(.Bits(3)) add_1 (.a({2'b00, parity[0]}), .b({2'b00, parity[1]}), .c_i(1'b0), .s(add_1_s));  // open: c_o
  Add #(.Bits(3)) add_2 (.a({2'b00, parity[2]}), .b({2'b00, parity[3]}), .c_i(1'b0), .s(add_2_s));  // open: c_o
  Add #(.Bits(3)) add_3 (.a(add_1_s), .b(add_2_s), .c_i(1'b0), .s(odd));  // open: c_o

  // Notes on the sheet:
  //   P60 Parity generator - Digital task
  //   XOR trees for each byte, then the totals.
  //   Allowed parts: all of the above + Add, Sub, Comparator, Neg
  //   Do not rename, move or delete the input and output pins.
endmodule

/* Test case public tests:
data parity odd
0 0 0
2147483648 24 1
6 0 0
4294967295 0 0
4148439348 27 3
2147483647 24 1
239220657 10 2
970787123 0 0
4294967295 0 0
2147483648 24 1
2879705167 15 4
2147483647 24 1
129895154 9 2
2779827643 6 2
10 0 0
2435568867 9 2
12 0 0
2147483647 24 1
2147483647 24 1
0 0 0
1619574146 0 0
23 0 0
13 17 1
27 0 0
9 0 0
2147483647 24 1
2954582114 27 3
16 17 1
4276573604 9 2
6 0 0
29 0 0
2318470418 30 3
4294967295 0 0
3673082515 24 1
2637214178 24 1
3380421899 3 2
3939897719 12 2
13 17 1
6 0 0
2147483647 24 1
3957709708 5 2
3396847646 18 1
4294967295 0 0
2147483648 24 1
2995875506 6 2
2307147247 27 3
2147483647 24 1
4117560749 3 2
635208612 15 4
2282922776 0 0
57831157 18 1
3898235288 17 1
2147483648 24 1
2600751558 30 3
1619594579 6 2
744410555 30 3
2147483648 24 1
432671881 9 2
2147483648 24 1
3325206942 23 3
186764559 10 2
1276417048 10 2
2775286204 5 2
3680839617 17 1
1433641979 5 2
2509347387 5 2
0 0 0
3238957777 30 3
3456685667 30 3
11 17 1
2627756702 3 2
3825538410 18 1
3421895856 9 2
182547048 17 1
0 0 0
2147483647 24 1
2 17 1
3861431416 10 2
3926494403 10 2
4 17 1
0 0 0
2 17 1
2147483647 24 1
1066875269 5 2
1237798108 15 4
0 0 0
1373444340 9 2
1038197672 9 2
2289507090 0 0
11 17 1
2147483647 24 1
9 0 0
774490716 20 1
1523498557 5 2
2057059732 27 3
2857843751 20 1
4294967295 0 0
0 0 0
18 0 0
878890485 30 3
130997592 29 3
3179853679 0 0
11 17 1
26 17 1
1923968481 6 2
648503758 15 4
2147483647 24 1
4294967295 0 0
2437908618 29 3
0 0 0
2898332814 20 1
71530862 15 4
24 0 0
16 17 1
282654850 10 2
3798280208 17 1
4169608042 24 1
814830966 5 2
0 0 0
7 17 1
1462173232 30 3
2147483648 24 1
2147483647 24 1
3185846339 17 1
4294967295 0 0
573792170 0 0
2345625831 18 1
0 0 0
4149056288 9 2
811103642 6 2
3347118968 30 3
1 17 1
4294192716 5 2
0 0 0
2147483647 24 1
0 0 0
680856159 0 0
1961940552 18 1
20 0 0
25 17 1
3466116670 29 3
1877760324 20 1
4294967295 0 0
805701350 17 1
879102481 24 1
24 0 0
2147483648 24 1
2147483648 24 1
11 17 1
3830100622 20 1
20 0 0
4294967295 0 0
4050407651 9 2
0 0 0
317623446 18 1
26 17 1
791486565 10 2
0 0 0
9 0 0
2507565199 23 3
*/
