// Digital circuit P63.dig as structural Verilog
module P63 (
  input  clk,
  input  rst,
  input  push,
  input  pop,
  input  [3:0] d,
  output [3:0] top,
  output [2:0] count,
  output empty,
  output full
);

  wire and_1_out, and_2_out, and_3_out, and_4_out, and_5_out, and_6_out, and_7_out, and_8_out, and_9_out,
       and_10_out, and_11_out, and_12_out, and_13_out, and_14_out, and_15_out, and_16_out, and_17_out,
       and_18_out, and_19_out, not_1_out, not_2_out, not_3_out, not_4_out, not_5_out, not_6_out, not_7_out,
       or_1_out, or_2_out, or_3_out, or_4_out, or_5_out, xor_1_out, xor_2_out, xor_3_out;
  wire [3:0] d_ff_4_q, d_ff_5_q, d_ff_6_q, d_ff_7_q, multiplexer_1_out, multiplexer_2_out, multiplexer_3_out,
       multiplexer_4_out, multiplexer_5_out, multiplexer_6_out, multiplexer_7_out;

  not not_1 (not_1_out, rst);
  not not_2 (not_2_out, pop);
  not not_3 (not_3_out, push);
  not not_4 (not_4_out, count[0]);
  not not_5 (not_5_out, count[1]);
  not not_6 (not_6_out, count[2]);
  not not_7 (not_7_out, empty);
  and and_1 (and_1_out, push, not_2_out);
  and and_2 (and_2_out, and_1_out, not_6_out);
  and and_3 (and_3_out, pop, not_3_out);
  and and_4 (and_4_out, and_3_out, not_7_out);
  and and_5 (and_5_out, and_2_out, count[0]);
  and and_6 (and_6_out, and_4_out, not_4_out);
  and and_7 (and_7_out, count[1], count[0]);
  and and_8 (and_8_out, not_5_out, not_4_out);
  and and_9 (and_9_out, not_5_out, count[0]);
  and and_10 (and_10_out, count[1], not_4_out);
  and and_11 (and_11_out, and_2_out, and_7_out);
  and and_12 (and_12_out, and_4_out, and_8_out);
  and and_13 (and_13_out, not_1_out, xor_1_out);
  and and_14 (and_14_out, not_1_out, xor_2_out);
  and and_15 (and_15_out, not_1_out, xor_3_out);
  and and_16 (and_16_out, and_2_out, and_8_out);
  and and_17 (and_17_out, and_2_out, and_9_out);
  and and_18 (and_18_out, and_2_out, and_10_out);
  and and_19 (and_19_out, and_2_out, and_7_out);
  or or_1 (or_1_out, count[0], count[1]);
  or or_2 (or_2_out, and_2_out, and_4_out);
  or or_3 (or_3_out, and_5_out, and_6_out);
  or or_4 (or_4_out, and_11_out, and_12_out);
  not not_8 (empty, or_5_out);
  or or_5 (or_5_out, or_1_out, count[2]);
  xor xor_1 (xor_1_out, count[0], or_2_out);
  xor xor_2 (xor_2_out, count[1], or_3_out);
  xor xor_3 (xor_3_out, count[2], or_4_out);
  D_FF #(.Bits(1)) d_ff_1 (.D(and_13_out), .C(clk), .Q(count[0]));  // open: nQ
  D_FF #(.Bits(1)) d_ff_2 (.D(and_14_out), .C(clk), .Q(count[1]));  // open: nQ
  D_FF #(.Bits(1)) d_ff_3 (.D(and_15_out), .C(clk), .Q(count[2]));  // open: nQ
  Multiplexer #(.Bits(4)) multiplexer_1 (.sel(and_16_out), .in_0(d_ff_4_q), .in_1(d), .out(multiplexer_1_out));
  D_FF #(.Bits(4)) d_ff_4 (.D(multiplexer_1_out), .C(clk), .Q(d_ff_4_q));  // open: nQ
  Multiplexer #(.Bits(4)) multiplexer_2 (.sel(and_17_out), .in_0(d_ff_5_q), .in_1(d), .out(multiplexer_2_out));
  D_FF #(.Bits(4)) d_ff_5 (.D(multiplexer_2_out), .C(clk), .Q(d_ff_5_q));  // open: nQ
  Multiplexer #(.Bits(4)) multiplexer_3 (.sel(and_18_out), .in_0(d_ff_6_q), .in_1(d), .out(multiplexer_3_out));
  D_FF #(.Bits(4)) d_ff_6 (.D(multiplexer_3_out), .C(clk), .Q(d_ff_6_q));  // open: nQ
  Multiplexer #(.Bits(4)) multiplexer_4 (.sel(and_19_out), .in_0(d_ff_7_q), .in_1(d), .out(multiplexer_4_out));
  D_FF #(.Bits(4)) d_ff_7 (.D(multiplexer_4_out), .C(clk), .Q(d_ff_7_q));  // open: nQ
  Multiplexer #(.Bits(4)) multiplexer_5 (.sel(count[0]), .in_0(d_ff_7_q), .in_1(d_ff_4_q), .out(multiplexer_5_out));
  Multiplexer #(.Bits(4)) multiplexer_6 (.sel(count[0]), .in_0(d_ff_5_q), .in_1(d_ff_6_q), .out(multiplexer_6_out));
  Multiplexer #(.Bits(4)) multiplexer_7 (
    .sel(count[1]), .in_0(multiplexer_5_out), .in_1(multiplexer_6_out), .out(multiplexer_7_out));
  Multiplexer #(.Bits(4)) multiplexer_8 (.sel(empty), .in_0(multiplexer_7_out), .in_1(4'b0000), .out(top));

  assign full = count[2];

  // Notes on the sheet:
  //   clk: Hz: 1
  //   P63 Hardware stack - Digital task
  //   4 entries x 4 bits with a stack pointer.
  //   Allowed parts: gates + multiplexer/decoder parts + flip-flops
  //   Do not rename, move or delete the input and output pins.
endmodule

/* Test case public tests:
clk rst push pop d top count empty full
C 1 0 0 1 0 0 1 0
C 0 0 1 15 0 0 1 0
C 0 1 0 7 7 1 0 0
C 0 1 0 15 15 2 0 0
C 1 0 1 3 0 0 1 0
C 0 1 1 6 0 0 1 0
C 1 0 1 3 0 0 1 0
C 0 1 0 2 2 1 0 0
C 0 0 0 0 2 1 0 0
C 0 1 1 3 2 1 0 0
C 0 0 1 9 0 0 1 0
C 0 1 1 15 0 0 1 0
C 0 1 0 12 12 1 0 0
C 0 0 0 13 12 1 0 0
C 0 1 0 11 11 2 0 0
C 0 0 0 8 11 2 0 0
C 0 1 0 6 6 3 0 0
C 0 0 1 10 11 2 0 0
C 0 0 0 3 11 2 0 0
C 0 0 0 2 11 2 0 0
C 0 1 1 15 11 2 0 0
C 0 0 1 7 12 1 0 0
C 0 0 0 5 12 1 0 0
C 0 1 1 8 12 1 0 0
C 0 1 1 5 12 1 0 0
C 0 1 1 13 12 1 0 0
C 0 0 1 12 0 0 1 0
C 0 0 0 12 0 0 1 0
C 0 0 0 15 0 0 1 0
C 0 0 0 15 0 0 1 0
C 0 0 0 15 0 0 1 0
C 0 0 1 7 0 0 1 0
C 0 0 0 3 0 0 1 0
C 0 1 0 0 0 1 0 0
C 1 0 1 0 0 0 1 0
C 0 1 0 11 11 1 0 0
C 0 0 1 10 0 0 1 0
C 0 0 1 2 0 0 1 0
C 0 0 1 11 0 0 1 0
C 0 1 0 12 12 1 0 0
C 0 0 1 14 0 0 1 0
C 0 0 0 10 0 0 1 0
C 0 1 1 11 0 0 1 0
C 0 1 1 15 0 0 1 0
C 0 1 1 5 0 0 1 0
C 0 1 1 4 0 0 1 0
C 0 1 1 15 0 0 1 0
C 0 1 0 7 7 1 0 0
C 0 0 1 10 0 0 1 0
C 0 0 0 5 0 0 1 0
C 0 1 1 14 0 0 1 0
C 0 1 0 4 4 1 0 0
C 0 0 0 6 4 1 0 0
C 0 1 1 7 4 1 0 0
C 0 0 0 4 4 1 0 0
C 0 1 0 12 12 2 0 0
C 0 1 0 14 14 3 0 0
C 0 0 0 1 14 3 0 0
C 0 0 0 10 14 3 0 0
C 0 1 1 5 14 3 0 0
C 0 0 1 15 12 2 0 0
C 0 0 0 4 12 2 0 0
C 0 1 1 11 12 2 0 0
C 0 1 0 1 1 3 0 0
C 0 1 1 7 1 3 0 0
C 0 0 1 1 12 2 0 0
C 0 0 1 7 4 1 0 0
C 0 0 0 5 4 1 0 0
C 0 0 0 0 4 1 0 0
C 0 0 1 3 0 0 1 0
C 0 0 0 4 0 0 1 0
C 0 1 1 13 0 0 1 0
C 0 0 1 8 0 0 1 0
C 1 1 1 8 0 0 1 0
C 0 1 0 15 15 1 0 0
C 0 0 0 5 15 1 0 0
C 0 0 1 6 0 0 1 0
C 0 1 1 13 0 0 1 0
C 0 0 0 9 0 0 1 0
C 0 0 1 11 0 0 1 0
C 0 1 1 10 0 0 1 0
C 0 1 0 11 11 1 0 0
C 0 1 1 11 11 1 0 0
C 0 1 1 8 11 1 0 0
C 0 1 0 14 14 2 0 0
C 0 1 1 6 14 2 0 0
C 0 0 1 7 11 1 0 0
C 0 0 0 6 11 1 0 0
C 0 0 0 8 11 1 0 0
C 0 1 0 0 0 2 0 0
C 0 1 0 0 0 3 0 0
C 0 1 0 12 12 4 0 1
C 0 1 1 4 12 4 0 1
C 0 1 0 9 12 4 0 1
C 0 1 0 2 12 4 0 1
C 0 0 0 11 12 4 0 1
C 0 1 0 1 12 4 0 1
C 0 1 0 3 12 4 0 1
C 0 1 1 3 12 4 0 1
C 0 0 1 9 0 3 0 0
C 0 0 1 10 0 2 0 0
C 0 0 0 14 0 2 0 0
C 0 1 0 9 9 3 0 0
C 0 0 0 7 9 3 0 0
C 0 1 1 11 9 3 0 0
C 0 1 0 0 0 4 0 1
C 0 0 1 1 9 3 0 0
C 0 0 1 8 0 2 0 0
C 0 1 1 0 0 2 0 0
C 0 1 0 8 8 3 0 0
C 0 0 0 13 8 3 0 0
C 0 0 1 15 0 2 0 0
C 0 1 0 2 2 3 0 0
C 0 0 0 5 2 3 0 0
C 0 0 0 7 2 3 0 0
C 0 1 1 0 2 3 0 0
C 0 1 1 15 2 3 0 0
C 0 1 0 15 15 4 0 1
C 0 0 1 0 2 3 0 0
C 0 1 0 1 1 4 0 1
C 0 0 1 7 2 3 0 0
C 0 1 1 15 2 3 0 0
C 0 0 0 7 2 3 0 0
C 0 0 0 2 2 3 0 0
C 0 1 1 7 2 3 0 0
C 0 0 1 13 0 2 0 0
C 0 0 0 0 0 2 0 0
C 0 0 0 0 0 2 0 0
C 0 1 1 7 0 2 0 0
C 0 0 1 7 11 1 0 0
C 0 1 0 2 2 2 0 0
C 0 0 0 15 2 2 0 0
C 0 1 1 7 2 2 0 0
C 0 1 1 14 2 2 0 0
C 0 1 1 11 2 2 0 0
C 0 0 0 2 2 2 0 0
C 0 0 0 11 2 2 0 0
C 0 1 1 15 2 2 0 0
C 0 1 0 6 6 3 0 0
C 0 1 1 4 6 3 0 0
C 0 1 0 8 8 4 0 1
C 0 0 0 8 8 4 0 1
C 0 1 0 13 8 4 0 1
C 0 1 0 6 8 4 0 1
C 0 0 0 3 8 4 0 1
C 0 0 0 13 8 4 0 1
C 0 0 1 7 6 3 0 0
C 0 1 0 7 7 4 0 1
C 0 1 1 7 7 4 0 1
C 0 1 1 0 7 4 0 1
C 0 0 0 0 7 4 0 1
C 0 1 1 4 7 4 0 1
C 0 0 1 14 6 3 0 0
C 0 0 0 13 6 3 0 0
C 0 0 1 0 2 2 0 0
C 0 1 0 13 13 3 0 0
C 0 0 0 13 13 3 0 0
C 0 0 0 6 13 3 0 0
C 0 1 0 8 8 4 0 1
C 0 0 0 7 8 4 0 1
*/
